// Logisim project zaid.circ as structural Verilog: 5 circuits, main circuit main
module main (
  input  in_1,
  input  in_2,
  input  in_3,
  output out_4,
  output out_5,
  output out_6,
  output out_7,
  output out_8,
  output out_9,
  output out_10,
  output out_11,
  output out_12,
  output out_13,
  output out_14,
  output out_15
);

  wire clock_1_out;
  wire [31:0] adder_1_out, register_1_q;
  wire [31:6] rom_1_data;

  Register #(.width(32)) register_1 (.D(adder_1_out), .en(in_1), .Q(register_1_q), .clk(clock_1_out), .clr(in_2));
  Clock clock_1 (.out(clock_1_out));
  // Probe on register_1_q
  Adder #(.width(32)) adder_1 (.a(register_1_q), .b(32'h4), .out(adder_1_out));  // open: cin, cout
  // Probe on {rom_1_data, {6{rom_1_data[6]}}}
  ROM #(.addrWidth(24), .dataWidth(32)) rom_1 (
    .addr(register_1_q[25:2]), .data({rom_1_data, {6{rom_1_data[6]}}}), .sel(in_3));
  // decoder decoder_1: pin names not known; wires that end beside it: rom_1_data[6], out_4, out_5, out_6, out_7, out_8, out_9, out_10, out_11, out_12, out_13, out_14
endmodule

module decoder (
  input  [31:0] _32_bit_instructions,
  output [6:0] opcode,
  output [4:0] rd,
  output [2:0] func_3,
  output [4:0] rs1,
  output [4:0] rs2,
  output [6:0] func_7
);


  assign func_3 = _32_bit_instructions[14:12];
  assign func_7 = _32_bit_instructions[31:25];
  assign opcode = _32_bit_instructions[6:0];
  assign rd = _32_bit_instructions[11:7];
  assign rs1 = _32_bit_instructions[19:15];
  assign rs2 = _32_bit_instructions[24:20];
endmodule

module opcode_i_type (
  input  [6:0] in_1,
  input  [2:0] in_2,
  input  [1:0] in_3,
  input  in_4,
  output ori,
  output lb,
  output andi,
  output lh,
  output jalr,
  output lw,
  output lbu,
  output lhu,
  output addi,
  output slli,
  output slti,
  output sltiu,
  output xori,
  output srli,
  output srai
);

  wire demultiplexer_2_out5, nand_1_out, nand_2_out, nand_3_out, nand_4_out, nand_5_out, nand_6_out,
       nand_7_out, nand_8_out, nand_9_out, nand_10_out, nand_11_out, nand_12_out, nand_13_out, nand_14_out,
       nand_15_out, nand_16_out, nand_17_out, nand_18_out, nand_19_out, nand_20_out, nand_21_out,
       nand_22_out, nand_23_out, nand_24_out, nand_25_out, nand_26_out, nand_27_out, nand_28_out,
       nand_29_out, nand_30_out, nand_31_out, nand_32_out, nand_33_out, nand_34_out, nand_35_out,
       nand_36_out, nand_37_out, nand_38_out, nand_39_out, nand_40_out, nand_41_out, nand_42_out,
       nand_43_out, nand_44_out, nand_45_out, nand_46_out, nand_47_out, nand_48_out, nand_49_out,
       nand_50_out, nand_51_out, nand_52_out, nand_53_out, nand_54_out, nand_55_out, nand_56_out,
       nand_57_out, nand_58_out, nand_59_out, nand_60_out, nand_61_out, nand_62_out, nand_63_out,
       nand_64_out, nand_65_out, nand_66_out, nand_71_out, nand_78_out, nand_79_out, nand_80_out,
       nand_81_out, nand_82_out, nand_83_out, nand_84_out, nand_85_out, nand_86_out, nand_87_out,
       nand_88_out, nand_89_out, nand_90_out, nand_91_out;

  nand nand_1 (nand_1_out, in_1[6], in_1[6]);
  nand nand_2 (nand_2_out, in_1[5], in_1[5]);
  nand nand_3 (nand_3_out, in_1[4], in_1[4]);
  nand nand_4 (nand_4_out, in_1[3], in_1[3]);
  nand nand_5 (nand_5_out, in_1[2], in_1[2]);
  nand nand_6 (nand_6_out, in_1[6], in_1[6]);
  nand nand_7 (nand_7_out, in_1[5], in_1[5]);
  nand nand_8 (nand_8_out, in_1[4], in_1[4]);
  nand nand_9 (nand_9_out, in_1[3], in_1[3]);
  nand nand_10 (nand_10_out, in_1[2], in_1[2]);
  nand nand_11 (nand_11_out, in_1[6], in_1[6]);
  nand nand_12 (nand_12_out, in_1[5], in_1[5]);
  nand nand_13 (nand_13_out, in_1[4], in_1[4]);
  nand nand_14 (nand_14_out, in_1[3], in_1[3]);
  nand nand_15 (nand_15_out, in_1[2], in_1[2]);
  nand nand_16 (nand_16_out, in_1[6], in_1[6]);
  nand nand_17 (nand_17_out, in_1[5], in_1[5]);
  nand nand_18 (nand_18_out, in_1[4], in_1[4]);
  nand nand_19 (nand_19_out, in_1[3], in_1[3]);
  nand nand_20 (nand_20_out, in_1[2], in_1[2]);
  nand nand_21 (nand_21_out, in_1[6], in_1[6]);
  nand nand_22 (nand_22_out, in_1[5], in_1[5]);
  nand nand_23 (nand_23_out, in_1[4], in_1[4]);
  nand nand_24 (nand_24_out, in_1[3], in_1[3]);
  nand nand_25 (nand_25_out, in_1[2], in_1[2]);
  nand nand_26 (nand_26_out, in_1[6], in_1[6]);
  nand nand_27 (nand_27_out, in_1[5], in_1[5]);
  nand nand_28 (nand_28_out, in_1[3], in_1[3]);
  nand nand_29 (nand_29_out, in_1[2], in_1[2]);
  nand nand_30 (nand_30_out, in_1[6], in_1[6]);
  nand nand_31 (nand_31_out, in_1[5], in_1[5]);
  nand nand_32 (nand_32_out, in_1[3], in_1[3]);
  nand nand_33 (nand_33_out, in_1[2], in_1[2]);
  nand nand_34 (nand_34_out, in_1[6], in_1[6]);
  nand nand_35 (nand_35_out, in_1[5], in_1[5]);
  nand nand_36 (nand_36_out, in_1[3], in_1[3]);
  nand nand_37 (nand_37_out, in_1[2], in_1[2]);
  nand nand_38 (nand_38_out, in_1[6], in_1[6]);
  nand nand_39 (nand_39_out, in_1[5], in_1[5]);
  nand nand_40 (nand_40_out, in_1[3], in_1[3]);
  nand nand_41 (nand_41_out, in_1[2], in_1[2]);
  nand nand_42 (nand_42_out, in_1[6], in_1[6]);
  nand nand_43 (nand_43_out, in_1[5], in_1[5]);
  nand nand_44 (nand_44_out, in_1[3], in_1[3]);
  nand nand_45 (nand_45_out, in_1[2], in_1[2]);
  nand nand_46 (nand_46_out, in_1[6], in_1[6]);
  nand nand_47 (nand_47_out, in_1[5], in_1[5]);
  nand nand_48 (nand_48_out, in_1[3], in_1[3]);
  nand nand_49 (nand_49_out, in_1[2], in_1[2]);
  nand nand_50 (nand_50_out, in_1[6], in_1[6]);
  nand nand_51 (nand_51_out, in_1[5], in_1[5]);
  nand nand_52 (nand_52_out, in_1[3], in_1[3]);
  nand nand_53 (nand_53_out, in_1[2], in_1[2]);
  nand nand_54 (nand_54_out, nand_1_out, nand_2_out, nand_3_out, nand_4_out, nand_5_out, in_1[1], in_1[0]);
  nand nand_55 (nand_55_out, nand_6_out, nand_7_out, nand_8_out, nand_9_out, nand_10_out, in_1[1], in_1[0]);
  nand nand_56 (nand_56_out, nand_11_out, nand_12_out, nand_13_out, nand_14_out, nand_15_out, in_1[1], in_1[0]);
  nand nand_57 (nand_57_out, nand_16_out, nand_17_out, nand_18_out, nand_19_out, nand_20_out, in_1[1], in_1[0]);
  nand nand_58 (nand_58_out, nand_21_out, nand_22_out, nand_23_out, nand_24_out, nand_25_out, in_1[1], in_1[0]);
  nand nand_59 (nand_59_out, nand_26_out, nand_27_out, in_1[4], nand_28_out, nand_29_out, in_1[1], in_1[0]);
  nand nand_60 (nand_60_out, nand_30_out, nand_31_out, in_1[4], nand_32_out, nand_33_out, in_1[1], in_1[0]);
  nand nand_61 (nand_61_out, nand_34_out, nand_35_out, in_1[4], nand_36_out, nand_37_out, in_1[1], in_1[0]);
  nand nand_62 (nand_62_out, nand_38_out, nand_39_out, in_1[4], nand_40_out, nand_41_out, in_1[1], in_1[0]);
  nand nand_63 (nand_63_out, nand_42_out, nand_43_out, in_1[4], nand_44_out, nand_45_out, in_1[1], in_1[0]);
  nand nand_64 (nand_64_out, nand_46_out, nand_47_out, in_1[4], nand_48_out, nand_49_out, in_1[1], in_1[0]);
  nand nand_65 (nand_65_out, nand_50_out, nand_51_out, in_1[4], nand_52_out, nand_53_out, in_1[1], in_1[0]);
  nand nand_66 (nand_66_out, nand_54_out, nand_54_out);
  nand nand_67 (nand_66_out, nand_55_out, nand_55_out);
  nand nand_68 (nand_66_out, nand_56_out, nand_56_out);
  nand nand_69 (nand_66_out, nand_57_out, nand_57_out);
  nand nand_70 (nand_66_out, nand_58_out, nand_58_out);
  nand nand_71 (nand_71_out, nand_59_out, nand_59_out);
  nand nand_72 (nand_71_out, nand_60_out, nand_60_out);
  nand nand_73 (nand_71_out, nand_61_out, nand_61_out);
  nand nand_74 (nand_71_out, nand_62_out, nand_62_out);
  nand nand_75 (nand_71_out, nand_63_out, nand_63_out);
  nand nand_76 (nand_71_out, nand_64_out, nand_64_out);
  nand nand_77 (nand_71_out, nand_65_out, nand_65_out);
  Demultiplexer #(.select(3), .enable("false")) demultiplexer_1 (
    .out0(lb), .out1(lh), .out2(lw), .out3(lbu), .out4(lhu), .in(nand_66_out), .sel(in_2));  // open: out5, out6, out7
  Demultiplexer #(.select(3), .enable("false")) demultiplexer_2 (
    .out0(addi), .out1(slli), .out2(slti), .out3(sltiu), .out4(xori), .out5(demultiplexer_2_out5),
    .out6(ori), .out7(andi), .in(nand_71_out), .sel(in_2));
  Demultiplexer #(.select(2), .enable("false")) demultiplexer_3 (
    .out0(srli), .out1(srai), .in(demultiplexer_2_out5), .sel(in_3));  // open: out2, out3
  nand nand_78 (nand_78_out, in_1[6], in_1[6]);
  nand nand_79 (nand_79_out, in_1[5], in_1[5]);
  nand nand_80 (nand_80_out, in_1[3], in_1[3]);
  nand nand_81 (nand_81_out, in_1[2], in_1[2]);
  nand nand_82 (nand_82_out, in_1[6], in_1[6]);
  nand nand_83 (nand_83_out, in_1[5], in_1[5]);
  nand nand_84 (nand_84_out, in_1[3], in_1[3]);
  nand nand_85 (nand_85_out, in_1[2], in_1[2]);
  nand nand_86 (nand_86_out, in_1[4], in_1[4]);
  nand nand_87 (nand_87_out, in_1[3], in_1[3]);
  nand nand_88 (nand_88_out, nand_78_out, nand_79_out, in_1[4], nand_80_out, nand_81_out, in_1[1], in_1[0]);
  nand nand_89 (nand_89_out, nand_82_out, nand_83_out, in_1[4], nand_84_out, nand_85_out, in_1[1], in_1[0]);
  nand nand_90 (nand_90_out, in_1[6], in_1[5], nand_86_out, nand_87_out, in_1[2], in_1[1], in_1[0]);
  nand nand_91 (nand_91_out, nand_88_out, nand_88_out);
  nand nand_92 (nand_91_out, nand_89_out, nand_89_out);
  nand nand_93 (jalr, nand_90_out, nand_90_out);

  // Other names for the same wires on the sheet: _14_12_FUNC_3[2:0] = in_2; _30_31_FUNC_7[1:0] = in_3; andiOut = andi;
  //   ENABLE = in_4; _0 = in_1[0]; _1 = in_1[1]; _2 = in_1[2]; _3 = in_1[3]; _4 = in_1[4]; _5 = in_1[5]; _6 = in_1[6];
  //   oriOut = ori
endmodule

module Control_Decoder (
);

  decoder decoder_1 ();  // open: _32_bit_instructions, opcode, rd, func_3, rs1, rs2, func_7
endmodule

module immediate_generation (
  input  [6:0] in_1,
  input  [31:0] in_2,
  output [31:0] out_3,
  output [31:0] out_4,
  output [31:0] out_5,
  output [31:0] out_6
);

  wire comparator_1_eq, comparator_2_eq, comparator_3_eq, comparator_4_eq, comparator_5_eq, comparator_6_eq,
       comparator_7_eq, or_1_out;
  wire [11:0] controlled_buffer_1_out, controlled_buffer_2_out, controlled_buffer_3_out;
  wire [15:0] undriven, undriven_2;

  Comparator #(.width(7)) comparator_1 (.a(7'b0000011), .b(in_1), .eq(comparator_1_eq));  // open: gt, lt
  Comparator #(.width(7)) comparator_2 (.a(7'b0010011), .b(in_1), .eq(comparator_2_eq));  // open: gt, lt
  Comparator #(.width(7)) comparator_3 (.a(7'b1100111), .b(in_1), .eq(comparator_3_eq));  // open: gt, lt
  Comparator #(.width(7)) comparator_4 (.a(7'b0100011), .b(in_1), .eq(comparator_4_eq));  // open: gt, lt
  Comparator #(.width(7)) comparator_5 (.a(7'b1100011), .b(in_1), .eq(comparator_5_eq));  // open: gt, lt
  Comparator #(.width(7)) comparator_6 (.a(7'b1101111), .b(in_1), .eq(comparator_6_eq));  // open: gt, lt
  Comparator #(.width(7)) comparator_7 (.a(7'b0110111), .b(in_1), .eq(comparator_7_eq));  // open: gt, lt
  or or_1 (or_1_out, comparator_1_eq, comparator_2_eq, comparator_3_eq);
  // Probe on {in_2[31:25], in_2[11:7]}
  assign controlled_buffer_1_out = or_1_out ? in_2[31:20] : 12'bz;  // Controlled_Buffer controlled_buffer_1
  assign controlled_buffer_2_out = comparator_4_eq ? {in_2[31:25], in_2[11:7]} : 12'bz;  // Controlled_Buffer controlled_buffer_2
  // Probe on controlled_buffer_3_out
  assign controlled_buffer_3_out = comparator_5_eq ? {in_2[12], in_2[30:25], in_2[10:7], in_2[11]} : 12'bz;  // Controlled_Buffer controlled_buffer_3
  assign out_6 = comparator_6_eq ? {undriven_2, undriven} : 32'bz;  // Controlled_Buffer controlled_buffer_4
  assign out_3 = {{20{controlled_buffer_1_out[11]}}, controlled_buffer_1_out};  // Bit_Extender bit_extender_1
  // Probe on out_4
  assign out_4 = {{20{controlled_buffer_2_out[11]}}, controlled_buffer_2_out};  // Bit_Extender bit_extender_2
  assign out_5 = {{20{controlled_buffer_3_out[11]}}, controlled_buffer_3_out};  // Bit_Extender bit_extender_3

  // Notes on the sheet:
  //   load i-type
  //   alu i-type
  //   jalr i-type
  //   store
  //   SB-type
  //   jal UJ-type
  //   auipc/lui U-type
endmodule
